# Fritzing sketch Circuito (saved by Fritzing 1.0.4)
breadboards: 1

parts:
  A1 = ESP32-C6-DevKitC-1
  GY1 = GY-521 (MPU-6050) [form="♀ (female)" package=THT]
  A2 = NEO-6M GPS Module [part_number=GY-GPS6MV2]

nets:
  N1: A1.Pin_1, GY1.pin1, A2.Vcc
  N2: A1.Pin_3, A2.Tx
  N3: A1.Pin_4, A2.Rx
  N4: A1.Pin_5, GY1.pin4
  N5: A1.Pin_6, GY1.pin3
  N6: A1.Pin_15, A1.Pin_18, A1.Pin_32, GY1.pin2, A2.GND

custom parts:
  ESP32-C6-DevKitC-1: ESP32-C6-DevKitC-1 is an entry-level development board based on ESP32-C6-WROOM-1(U), a general-purpose module with a 8 MB SPI flash. This board integrates complete Wi-Fi, Bluetooth LE, Zigbee, and Thread functions.
  GY-521 (MPU-6050): Placa GY-521 basada en conjunto de acelerómetro+giroscopios MPU-6050
  NEO-6M GPS Module: GY-GPS6MV2 NEO-6M GPS Module Module based on U-blox NEO-6M GPS engine, incorporating regulator for 3.3-5V DC input, MS621FE-compatible rechargeable battery for backup and EEPROM for storing configuration settings. Links: NEO-6 series product information page NEO-6 Datasheet
